# Fritzing sketch Esp32-CC1101-Standalone (saved by Fritzing 0.9.6b)

parts:
  MH-ET_Live_Minikit_for_ESP1 = MH-ET Live Minikit for ESP32
  M1 = cc1101 module
  TP2 = TP4056 [chip_label=TP4056 package="DIP (Dual Inline) [THT]"]
  Bat2 = battery_holder_single_18650
  S1 = Pushbutton [package="[SMD]"]
  S2 = Pushbutton [package="[SMD]"]
  S3 = Pushbutton [package="[SMD]"]
  S4 = Pushbutton [package="[SMD]"]
  U3 = SWITCH_SPDT [package=kps-1290]
  LED1 = smd LED [color="Red (633nm)" package="0805 [SMD]"]
  LED2 = smd LED [color="Red (633nm)" package="0805 [SMD]"]

nets:
  N1: MH-ET_Live_Minikit_for_ESP1.GND, M1.pin_9, M1.pin_10, TP2.pin6, LED1.cathode, LED2.cathode
  N2: MH-ET_Live_Minikit_for_ESP1.IO33, LED1.anode
  N3: MH-ET_Live_Minikit_for_ESP1.TMS, MH-ET_Live_Minikit_for_ESP1.VCC, MH-ET_Live_Minikit_for_ESP1.IO27, MH-ET_Live_Minikit_for_ESP1.IO25, MH-ET_Live_Minikit_for_ESP1.IO32, S1.Pin_3, S1.Pin_4, S2.Pin_3, S2.Pin_4, S3.Pin_3, S3.Pin_4, S4.Pin_3, S4.Pin_4
  N4: MH-ET_Live_Minikit_for_ESP1.IO26, LED2.anode
  N5: MH-ET_Live_Minikit_for_ESP1.IO18, M1.pin_4
  N6: MH-ET_Live_Minikit_for_ESP1.IO19, M1.pin_5
  N7: MH-ET_Live_Minikit_for_ESP1.IO23, M1.pin_3
  N8: MH-ET_Live_Minikit_for_ESP1.IO5, M1.pin_7
  N9: MH-ET_Live_Minikit_for_ESP1.3.3V, M1.pin_1, M1.pin_2, U3.P
  N10: MH-ET_Live_Minikit_for_ESP1.TDI, M1.pin_8
  N11: MH-ET_Live_Minikit_for_ESP1.IO4, M1.pin_6
  N12: TP2.pin3, U3.S
  N13: TP2.pin4, Bat2.+#1
  N14: TP2.pin5, Bat2.+#0

custom parts:
  MH-ET Live Minikit for ESP32: MH-ET Live Minikit for ESP32 ( http://mh.nodebb.com/topic/8/mh-et-live-minikit-for-esp32/2/) PCB footprint is invalid.
  cc1101 module: CC1101 rf module.
  TP4056: A DIP stand-in part for whatever IC you want. With 6 pins on a 300mil dual inline package (DIP) footprint.
  battery_holder_single_18650: single 18650 battery holder
